# Fritzing sketch Mux (saved by Fritzing 0.9.3b)
breadboards: 1

parts:
  Cmod_A1 = Cmod A7
  SW1 = DIP Switch 8 Position [package=dipswitch-08]
  LED1 = smd LED [color="Red (633nm)" package="1206 [SMD]"]
  R1 = Resistor [tolerance=±5% resistance=100 package=THT]
  R2 = Resistor [tolerance=±5% resistance=10k package=THT]
  R3 = Resistor [tolerance=±5% resistance=10k package=THT]
  R4 = Resistor [tolerance=±5% resistance=10k package=THT]

nets:
  N1: Cmod_A1.1, LED1.anode
  N2: Cmod_A1.V, SW1.14, SW1.15, SW1.16
  N3: Cmod_A1.7, SW1.1, R3.Pin_1
  N4: Cmod_A1.8, SW1.2, R2.Pin_1
  N5: Cmod_A1.9, SW1.3, R4.Pin_1
  N6: Cmod_A1.G, R1.Pin_0, R2.Pin_0, R3.Pin_0, R4.Pin_0
  N7: LED1.cathode, R1.Pin_1

notes:
  10kΩ
  100Ω

custom parts:
  Cmod A7: The Digilent Cmod A7 is a small, 48-pin DIP form factor board built around a Xilinx Artix 7 FPGA. The board also includes a USB-JTAG programming circuit, USB-UART bridge, clock source, Pmod host connector, SRAM, Quad SPI Flash, and basic I/O devices. These components make it a formidable, albeit compact, platform for digital logic circuits and Microblaze embedded softcore processor designs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
