# Fritzing sketch IntegerArithmetic_breadboard (saved by Fritzing 0.9.3b)
breadboards: 1

parts:
  Cmod_A1 = Cmod A7
  SW1 = DIP Switch 8 Position [package=dipswitch-08]
  LED1 = smd LED [color="Red (633nm)" package="1206 [SMD]"]
  R1 = Resistor [tolerance=±5% resistance=100 package=THT]
  LED2 = smd LED [color="Red (633nm)" package="1206 [SMD]"]
  R4 = Resistor [tolerance=±5% resistance=100 package=THT]
  R5 = Resistor [tolerance=±5% resistance=100 package=THT]
  R6 = Resistor [tolerance=±5% resistance=100 package=THT]
  LED3 = smd LED [color="Red (633nm)" package="1206 [SMD]"]
  LED4 = smd LED [color="Red (633nm)" package="1206 [SMD]"]
  R7 = Resistor [tolerance=±5% resistance=10k package=THT]
  R8 = Resistor [tolerance=±5% resistance=10k package=THT]
  R9 = Resistor [tolerance=±5% resistance=10k package=THT]
  R10 = Resistor [tolerance=±5% resistance=10k package=THT]
  R11 = Resistor [tolerance=±5% resistance=10k package=THT]
  R12 = Resistor [tolerance=±5% resistance=10k package=THT]
  R13 = Resistor [tolerance=±5% resistance=10k package=THT]
  R14 = Resistor [tolerance=±5% resistance=10k package=THT]
  LED5 = smd LED [color="Red (633nm)" package="1206 [SMD]"]
  LED6 = smd LED [color="Red (633nm)" package="1206 [SMD]"]
  LED7 = smd LED [color="Red (633nm)" package="1206 [SMD]"]
  LED8 = smd LED [color="Red (633nm)" package="1206 [SMD]"]
  R15 = Resistor [tolerance=±5% resistance=100 package=THT]
  R16 = Resistor [tolerance=±5% resistance=100 package=THT]
  R17 = Resistor [tolerance=±5% resistance=100 package=THT]
  R18 = Resistor [tolerance=±5% resistance=100 package=THT]

nets:
  N1: Cmod_A1.1, SW1.4, R13.Pin_1
  N2: Cmod_A1.2, SW1.3, R12.Pin_1
  N3: Cmod_A1.3, SW1.2, R11.Pin_1
  N4: Cmod_A1.4, SW1.1, R7.Pin_1
  N5: Cmod_A1.V, SW1.9, SW1.10, SW1.11, SW1.12, SW1.13, SW1.14, SW1.15, SW1.16
  N6: Cmod_A1.D1, LED8.anode
  N7: Cmod_A1.D2, LED7.anode
  N8: Cmod_A1.D3, LED6.anode
  N9: Cmod_A1.D4, LED5.anode
  N10: Cmod_A1.D5, LED1.anode
  N11: Cmod_A1.D6, LED2.anode
  N12: Cmod_A1.D7, LED3.anode
  N13: Cmod_A1.D8, LED4.anode
  N14: Cmod_A1.7, SW1.8, R8.Pin_1
  N15: Cmod_A1.8, SW1.7, R9.Pin_1
  N16: Cmod_A1.9, SW1.6, R10.Pin_1
  N17: Cmod_A1.10, SW1.5, R14.Pin_1
  N18: Cmod_A1.G, R1.Pin_0, R4.Pin_0, R5.Pin_0, R6.Pin_0, R7.Pin_0, R8.Pin_0, R9.Pin_0, R10.Pin_0, R11.Pin_0, R12.Pin_0, R13.Pin_0, R14.Pin_0, R15.Pin_0, R16.Pin_0, R17.Pin_0, R18.Pin_0
  N19: LED1.cathode, R15.Pin_1
  N20: R1.Pin_1, LED8.cathode
  N21: LED2.cathode, R16.Pin_1
  N22: R4.Pin_1, LED7.cathode
  N23: R5.Pin_1, LED6.cathode
  N24: R6.Pin_1, LED5.cathode
  N25: LED3.cathode, R17.Pin_1
  N26: LED4.cathode, R18.Pin_1

notes:
  10kΩ
  100Ω

custom parts:
  Cmod A7: The Digilent Cmod A7 is a small, 48-pin DIP form factor board built around a Xilinx Artix 7 FPGA. The board also includes a USB-JTAG programming circuit, USB-UART bridge, clock source, Pmod host connector, SRAM, Quad SPI Flash, and basic I/O devices. These components make it a formidable, albeit compact, platform for digital logic circuits and Microblaze embedded softcore processor designs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
