# Fritzing sketch LED_TactileSwitch (saved by Fritzing 0.9.3b)
breadboards: 1

parts:
  Cmod_A1 = Cmod A7
  LED1 = smd LED [color="Red (633nm)" package="1206 [SMD]"]
  R1 = Resistor [tolerance=±5% resistance=100 package=THT]
  R2 = Resistor [tolerance=±5% resistance=10k package=THT]
  S1 = Pushbutton [package="[THT]"]

nets:
  N1: Cmod_A1.1, R1.Pin_0
  N2: Cmod_A1.2, R2.Pin_0, S1.Pin_1, S1.Pin_2
  N3: Cmod_A1.V, S1.Pin_3, S1.Pin_4
  N4: Cmod_A1.G, LED1.cathode, R2.Pin_1
  N5: LED1.anode, R1.Pin_1

notes:
  10kΩ
  100Ω

custom parts:
  Cmod A7: The Digilent Cmod A7 is a small, 48-pin DIP form factor board built around a Xilinx Artix 7 FPGA. The board also includes a USB-JTAG programming circuit, USB-UART bridge, clock source, Pmod host connector, SRAM, Quad SPI Flash, and basic I/O devices. These components make it a formidable, albeit compact, platform for digital logic circuits and Microblaze embedded softcore processor designs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
