# Fritzing sketch Seg7LED_DipSwitch (saved by Fritzing 0.9.3b)
breadboards: 2

parts:
  SW1 = DIP Switch 8 Position [package=dipswitch-08]
  R8 = Resistor [tolerance=±5% resistance=100 package=THT]
  R9 = Resistor [tolerance=±5% resistance=100 package=THT]
  R10 = Resistor [tolerance=±5% resistance=100 package=THT]
  R11 = Resistor [tolerance=±5% resistance=100 package=THT]
  R12 = Resistor [tolerance=±5% resistance=100 package=THT]
  R13 = Resistor [tolerance=±5% resistance=100 package=THT]
  R14 = Resistor [tolerance=±5% resistance=100 package=THT]
  SW2 = DIP Switch 8 Position [package=dipswitch-08]
  R7 = Resistor [tolerance=±5% resistance=100 package=THT]
  R15 = Resistor [tolerance=±5% resistance=100 package=THT]
  R16 = Resistor [tolerance=±5% resistance=100 package=THT]
  R17 = Resistor [tolerance=±5% resistance=100 package=THT]
  R18 = Resistor [tolerance=±5% resistance=100 package=THT]
  R19 = Resistor [tolerance=±5% resistance=100 package=THT]
  R20 = Resistor [tolerance=±5% resistance=100 package=THT]
  R21 = Resistor [tolerance=±5% resistance=100 package=THT]
  R22 = Resistor [tolerance=±5% resistance=100 package=THT]
  Cmod_A1 = Cmod A7
  R30 = Resistor [tolerance=±5% resistance=10k package=THT]
  7_Segment_4_Digit_Display1 = 7-SEGMENT-4DIGIT common anode [part_number="5461BS - 5462BS" package=7-segment-4digit-anode]
  R31 = Resistor [tolerance=±5% resistance=10k package=THT]
  R32 = Resistor [tolerance=±5% resistance=10k package=THT]
  R33 = Resistor [tolerance=±5% resistance=10k package=THT]
  R34 = Resistor [tolerance=±5% resistance=10k package=THT]
  R35 = Resistor [tolerance=±5% resistance=10k package=THT]
  R36 = Resistor [tolerance=±5% resistance=10k package=THT]

nets:
  N1: SW1.1, R7.Pin_1, Cmod_A1.D48
  N2: SW1.2, R11.Pin_1, Cmod_A1.D47
  N3: SW1.3, R12.Pin_1, Cmod_A1.D46
  N4: SW1.4, R13.Pin_1, Cmod_A1.D45
  N5: SW1.5, R14.Pin_1, Cmod_A1.D44
  N6: SW1.6, R10.Pin_1, Cmod_A1.D43
  N7: SW1.7, R9.Pin_1, Cmod_A1.D42
  N8: SW1.8, R8.Pin_1, Cmod_A1.D41
  N9: SW1.9, SW1.10, SW1.11, SW1.12, SW1.13, SW1.14, SW1.15, SW1.16, SW2.9, SW2.10, SW2.11, SW2.12, SW2.13, SW2.14, SW2.15, SW2.16, Cmod_A1.V
  N10: R8.Pin_0, R9.Pin_0, R10.Pin_0, R11.Pin_0, R12.Pin_0, R13.Pin_0, R14.Pin_0, R7.Pin_0, R15.Pin_0, R16.Pin_0, R17.Pin_0, R18.Pin_0, R19.Pin_0, R20.Pin_0, R21.Pin_0, R22.Pin_0, Cmod_A1.G
  N11: SW2.1, R15.Pin_1, Cmod_A1.D40
  N12: SW2.2, R16.Pin_1, Cmod_A1.D39
  N13: SW2.3, R17.Pin_1, Cmod_A1.D38
  N14: SW2.4, R18.Pin_1, Cmod_A1.D37
  N15: SW2.5, R19.Pin_1, Cmod_A1.D36
  N16: SW2.6, R20.Pin_1, Cmod_A1.D35
  N17: SW2.7, R21.Pin_1, Cmod_A1.D34
  N18: SW2.8, R22.Pin_1, Cmod_A1.D33
  N19: Cmod_A1.1, 7_Segment_4_Digit_Display1.pin_6
  N20: Cmod_A1.2, 7_Segment_4_Digit_Display1.pin_8
  N21: Cmod_A1.3, 7_Segment_4_Digit_Display1.pin_9
  N22: Cmod_A1.4, 7_Segment_4_Digit_Display1.pin_12
  N23: Cmod_A1.D1, R36.Pin_1
  N24: Cmod_A1.D2, R35.Pin_1
  N25: Cmod_A1.D3, R34.Pin_1
  N26: Cmod_A1.D4, R33.Pin_1
  N27: Cmod_A1.D5, R32.Pin_1
  N28: Cmod_A1.D6, R31.Pin_1
  N29: Cmod_A1.D7, R30.Pin_1
  N30: R30.Pin_0, 7_Segment_4_Digit_Display1.pin_11
  N31: 7_Segment_4_Digit_Display1.pin_1, R34.Pin_0
  N32: 7_Segment_4_Digit_Display1.pin_2, R33.Pin_0
  N33: 7_Segment_4_Digit_Display1.pin_4, R32.Pin_0
  N34: 7_Segment_4_Digit_Display1.pin_5, R36.Pin_0
  N35: 7_Segment_4_Digit_Display1.pin_7, R31.Pin_0
  N36: 7_Segment_4_Digit_Display1.pin_10, R35.Pin_0

notes:
  10kΩ
  100Ω

custom parts:
  Cmod A7: The Digilent Cmod A7 is a small, 48-pin DIP form factor board built around a Xilinx Artix 7 FPGA. The board also includes a USB-JTAG programming circuit, USB-UART bridge, clock source, Pmod host connector, SRAM, Quad SPI Flash, and basic I/O devices. These components make it a formidable, albeit compact, platform for digital logic circuits and Microblaze embedded softcore processor designs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
  7-SEGMENT-4DIGIT common anode: A 7 Segment 4 Digit common anode display, with decimal points
