# Fritzing sketch KitchenTimer (saved by Fritzing 0.9.3b)
breadboards: 2

parts:
  Cmod_A1 = Cmod A7
  R30 = Resistor [tolerance=±5% resistance=100 package=THT]
  7_Segment_4_Digit_Display1 = 7-SEGMENT-4DIGIT common anode [part_number="5461BS - 5462BS" package=7-segment-4digit-anode]
  R31 = Resistor [tolerance=±5% resistance=100 package=THT]
  R32 = Resistor [tolerance=±5% resistance=100 package=THT]
  R33 = Resistor [tolerance=±5% resistance=100 package=THT]
  R34 = Resistor [tolerance=±5% resistance=100 package=THT]
  R35 = Resistor [tolerance=±5% resistance=100 package=THT]
  R36 = Resistor [tolerance=±5% resistance=100 package=THT]
  S1 = Pushbutton [package="[THT]"]
  S2 = Pushbutton [package="[THT]"]
  S3 = Pushbutton [package="[THT]"]
  R37 = Resistor [tolerance=±5% resistance=10k package=THT]
  R38 = Resistor [tolerance=±5% resistance=10k package=THT]
  R39 = Resistor [tolerance=±5% resistance=10k package=THT]
  R40 = Resistor [tolerance=±5% resistance=100 package=THT]

nets:
  N1: Cmod_A1.1, 7_Segment_4_Digit_Display1.pin_6
  N2: Cmod_A1.2, 7_Segment_4_Digit_Display1.pin_8
  N3: Cmod_A1.3, 7_Segment_4_Digit_Display1.pin_9
  N4: Cmod_A1.4, 7_Segment_4_Digit_Display1.pin_12
  N5: Cmod_A1.V, S1.Pin_1, S1.Pin_2, S2.Pin_1, S2.Pin_2, S3.Pin_1, S3.Pin_2
  N6: Cmod_A1.D1, R36.Pin_1
  N7: Cmod_A1.D2, R35.Pin_1
  N8: Cmod_A1.D3, R34.Pin_1
  N9: Cmod_A1.D4, R33.Pin_1
  N10: Cmod_A1.D5, R32.Pin_1
  N11: Cmod_A1.D6, R31.Pin_1
  N12: Cmod_A1.D7, R30.Pin_1
  N13: Cmod_A1.D8, R40.Pin_0
  N14: Cmod_A1.7, S1.Pin_3, S1.Pin_4, R37.Pin_0
  N15: Cmod_A1.8, S2.Pin_3, S2.Pin_4, R39.Pin_0
  N16: Cmod_A1.9, S3.Pin_3, S3.Pin_4, R38.Pin_0
  N17: Cmod_A1.G, R37.Pin_1, R38.Pin_1, R39.Pin_1
  N18: R30.Pin_0, 7_Segment_4_Digit_Display1.pin_11
  N19: 7_Segment_4_Digit_Display1.pin_1, R34.Pin_0
  N20: 7_Segment_4_Digit_Display1.pin_2, R33.Pin_0
  N21: 7_Segment_4_Digit_Display1.pin_3, R40.Pin_1
  N22: 7_Segment_4_Digit_Display1.pin_4, R32.Pin_0
  N23: 7_Segment_4_Digit_Display1.pin_5, R36.Pin_0
  N24: 7_Segment_4_Digit_Display1.pin_7, R31.Pin_0
  N25: 7_Segment_4_Digit_Display1.pin_10, R35.Pin_0

notes:
  分
  秒
  スタート・ストップ
  10kΩ
  100Ω

custom parts:
  Cmod A7: The Digilent Cmod A7 is a small, 48-pin DIP form factor board built around a Xilinx Artix 7 FPGA. The board also includes a USB-JTAG programming circuit, USB-UART bridge, clock source, Pmod host connector, SRAM, Quad SPI Flash, and basic I/O devices. These components make it a formidable, albeit compact, platform for digital logic circuits and Microblaze embedded softcore processor designs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
  7-SEGMENT-4DIGIT common anode: A 7 Segment 4 Digit common anode display, with decimal points
