# Fritzing sketch JoyStick (saved by Fritzing 0.9.3b)
breadboards: 2

parts:
  Cmod_A1 = Cmod A7
  R30 = Resistor [tolerance=±5% resistance=100 package=THT]
  7_Segment_4_Digit_Display1 = 7-SEGMENT-4DIGIT common anode [part_number="5461BS - 5462BS" package=7-segment-4digit-anode]
  R31 = Resistor [tolerance=±5% resistance=100 package=THT]
  R32 = Resistor [tolerance=±5% resistance=100 package=THT]
  R33 = Resistor [tolerance=±5% resistance=100 package=THT]
  R34 = Resistor [tolerance=±5% resistance=100 package=THT]
  R35 = Resistor [tolerance=±5% resistance=100 package=THT]
  R36 = Resistor [tolerance=±5% resistance=100 package=THT]
  R40 = Resistor [tolerance=±5% resistance=100 package=THT]
  ADC1 = MCP3008 [package=dil16]
  パーツ1 = Parallax 2-Axis Joystick

nets:
  N1: Cmod_A1.1, 7_Segment_4_Digit_Display1.pin_6
  N2: Cmod_A1.2, 7_Segment_4_Digit_Display1.pin_8
  N3: Cmod_A1.3, 7_Segment_4_Digit_Display1.pin_9
  N4: Cmod_A1.4, 7_Segment_4_Digit_Display1.pin_12
  N5: Cmod_A1.V, ADC1.VREF, ADC1.VDD, パーツ1.U/D_Vcc
  N6: Cmod_A1.D1, R36.Pin_1
  N7: Cmod_A1.D2, R35.Pin_1
  N8: Cmod_A1.D3, R34.Pin_1
  N9: Cmod_A1.D4, R33.Pin_1
  N10: Cmod_A1.D5, R32.Pin_1
  N11: Cmod_A1.D6, R31.Pin_1
  N12: Cmod_A1.D7, R30.Pin_1
  N13: Cmod_A1.D8, R40.Pin_0
  N14: Cmod_A1.7, ADC1.CLK
  N15: Cmod_A1.8, ADC1.Dout
  N16: Cmod_A1.9, ADC1.Din
  N17: Cmod_A1.10, ADC1.CS/SHDN
  N18: Cmod_A1.G, ADC1.DGND, ADC1.AGND, パーツ1.GND#8
  N19: R30.Pin_0, 7_Segment_4_Digit_Display1.pin_11
  N20: 7_Segment_4_Digit_Display1.pin_1, R34.Pin_0
  N21: 7_Segment_4_Digit_Display1.pin_2, R33.Pin_0
  N22: 7_Segment_4_Digit_Display1.pin_3, R40.Pin_1
  N23: 7_Segment_4_Digit_Display1.pin_4, R32.Pin_0
  N24: 7_Segment_4_Digit_Display1.pin_5, R36.Pin_0
  N25: 7_Segment_4_Digit_Display1.pin_7, R31.Pin_0
  N26: 7_Segment_4_Digit_Display1.pin_10, R35.Pin_0
  N27: ADC1.CH0, パーツ1.U/D_Out

notes:
  100Ω

custom parts:
  Cmod A7: The Digilent Cmod A7 is a small, 48-pin DIP form factor board built around a Xilinx Artix 7 FPGA. The board also includes a USB-JTAG programming circuit, USB-UART bridge, clock source, Pmod host connector, SRAM, Quad SPI Flash, and basic I/O devices. These components make it a formidable, albeit compact, platform for digital logic circuits and Microblaze embedded softcore processor designs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
  7-SEGMENT-4DIGIT common anode: A 7 Segment 4 Digit common anode display, with decimal points
  Parallax 2-Axis Joystick: Description: This is the Parallax 2-Axis Joystick. It contains a spring return thumb joystick mounted to a breakout board. The breakout board breaks out the joysticks connections to .1" pin headers. The joystick's connections are duplicated on both sides of the board for easy use. This part can easily be used on a breadboard due to the .1" pin headers, but can also be soldered into any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
