# Fritzing sketch ServoMotor (saved by Fritzing 0.9.3b)
breadboards: 1

parts:
  Cmod_A1 = Cmod A7
  ADC1 = MCP3008 [package=dil16]
  パーツ1 = Parallax 2-Axis Joystick
  VCC1 = 4 x AAA Battery Mount
  J1 = Basic Servo
  J2 = Basic Servo

nets:
  N1: Cmod_A1.1, J1.pulse
  N2: Cmod_A1.2, J2.pulse
  N3: Cmod_A1.V, ADC1.VREF, ADC1.VDD, パーツ1.U/D_Vcc
  N4: Cmod_A1.7, ADC1.CLK
  N5: Cmod_A1.8, ADC1.Dout
  N6: Cmod_A1.9, ADC1.Din
  N7: Cmod_A1.10, ADC1.CS/SHDN
  GND: Cmod_A1.G, ADC1.DGND, ADC1.AGND, パーツ1.GND#8, VCC1.-, J1.gnd, J2.gnd
  N8: ADC1.CH0, パーツ1.U/D_Out
  VCC: VCC1.+, J1.vcc, J2.vcc

notes:
  アルカリ単３x ３本

custom parts:
  Cmod A7: The Digilent Cmod A7 is a small, 48-pin DIP form factor board built around a Xilinx Artix 7 FPGA. The board also includes a USB-JTAG programming circuit, USB-UART bridge, clock source, Pmod host connector, SRAM, Quad SPI Flash, and basic I/O devices. These components make it a formidable, albeit compact, platform for digital logic circuits and Microblaze embedded softcore processor designs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
  Parallax 2-Axis Joystick: Description: This is the Parallax 2-Axis Joystick. It contains a spring return thumb joystick mounted to a breakout board. The breakout board breaks out the joysticks connections to .1" pin headers. The joystick's connections are duplicated on both sides of the board for easy use. This part can easily be used on a breadboard due to the .1" pin headers, but can also be soldered into any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
