# Fritzing sketch LCDDisplay (saved by Fritzing 0.9.3b)
breadboards: 1

parts:
  Cmod_A1 = Cmod A7
  IC1 = 2.8 inch LCD SPI display with touch screen & SD card

nets:
  N1: Cmod_A1.1, IC1.pin3
  N2: Cmod_A1.2, IC1.pin4
  N3: Cmod_A1.3, IC1.pin5
  N4: Cmod_A1.4, IC1.pin6
  N5: Cmod_A1.V, IC1.pin1
  N6: Cmod_A1.7, IC1.pin7
  N7: Cmod_A1.8, IC1.pin8
  N8: Cmod_A1.9, IC1.pin_9
  N9: Cmod_A1.G, IC1.pin2

custom parts:
  Cmod A7: The Digilent Cmod A7 is a small, 48-pin DIP form factor board built around a Xilinx Artix 7 FPGA. The board also includes a USB-JTAG programming circuit, USB-UART bridge, clock source, Pmod host connector, SRAM, Quad SPI Flash, and basic I/O devices. These components make it a formidable, albeit compact, platform for digital logic circuits and Microblaze embedded softcore processor designs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
  2.8 inch LCD SPI display with touch screen & SD card: A generic 2.8 inch LCD TFT 320x280 display with touchscreen and SD card slot.
