# Fritzing sketch Crawler (saved by Fritzing 0.9.3b)
breadboards: 2

parts:
  M1 = DC Motor
  IC1 = AE-DRV8835-S [package="DIP (Dual Inline) [THT]"]
  VCC1 = Battery
  M2 = DC Motor
  ADC1 = MCP3008 [package=dil16]
  R1 = PHOTOCELL [package=photocell-kit]
  R2 = PHOTOCELL [package=photocell-kit]
  R3 = Resistor [tolerance=±5% resistance=220 package=THT]
  R4 = Resistor [tolerance=±5% resistance=220 package=THT]

nets:
  N1: M1.pin_1, IC1.AOUT2
  N2: M1.pin_2, IC1.AOUT1
  N3: IC1.VM, VCC1.+
  N4: IC1.BOUT1, M2.pin_2
  N5: IC1.BOUT2, M2.pin_1
  N6: IC1.GND, IC1.MODE, VCC1.-, ADC1.DGND, ADC1.AGND, R3.Pin_1, R4.Pin_1
  VCC: IC1.VCC, ADC1.VREF, ADC1.VDD, R1.P$1, R2.P$2
  N7: ADC1.CH0, R1.P$2, R3.Pin_0
  N8: ADC1.CH1, R2.P$1, R4.Pin_0

notes:
  AN1, AN2, BN1, BN2
  CLK, Dout, Din, CSn

custom parts:
  AE-DRV8835-S: A DRV8835 breakout board by Akizuki Denshi Tsusho Co.,Ltd.
